# Fritzing sketch ADXL345_to_WTV020_to_trigger_audio_V2_ino (saved by Fritzing 0.8.3b)
breadboards: 1

parts:
  IC1 = IC, DIP package, 16 pins [chip_label=WTV020 part_number=WTV020]
  Part1 = Arduino Uno (Rev3)
  IC6 = IC, DIP package, 10 pins [chip_label=ADXL345]
  SP1 = SPEAKER [package=pcb_mount_speaker]
  LED1 = LED - 5mm [color="Yellow (595nm)" package="5 mm [THT]"]
  R2 = Resistor [tolerance=±5% resistance=220 package=THT]

nets:
  N1: IC1.pin4, SP1.-
  N2: IC1.pin5, SP1.+
  N3: IC1.pin7, Part1.D3_PWM
  N4: IC1.pin8, Part1.GND, IC6.pin8
  N5: IC1.pin10, Part1.D6_PWM
  N6: IC1.pin15, Part1.D7, LED1.cathode
  N7: Part1.A4/SDA, IC6.pin2
  N8: Part1.A5/SCL, IC6.pin1
  N9: Part1.3V3, IC6.pin9, R2.Pin_1
  N10: LED1.anode, R2.Pin_0
